# Fritzing sketch RTII-ReactionTimeExercise-~1 (saved by Fritzing 0.9.3b)
breadboards: 1

parts:
  Part3 = Arduino Uno (Rev3)
  S2 = Pushbutton [package="[THT]"]
  R8 = Resistor [tolerance=±5% resistance=12k package=THT]
  Q4 = Basic FET N-Channel [package="DPak [SMD]"]
  R10 = Resistor [tolerance=±5% resistance=12 package=THT]
  D3 = Diode [package=diode-hv]
  R11 = Resistor [tolerance=±5% resistance=12k package="0805 [SMD]"]
  U3 = Vibration Motor- ROB-08449 [package=vibe-motor-10mm]
  R15 = Resistor [tolerance=±5% resistance=220 package=THT]
  LED3 = LED - 5mm [color="Yellow (592nm)" package="5 mm [THT]"]

nets:
  N1: Part3.D11_PWM/MOSI, LED3.cathode
  N2: Part3.D12/MISO, S2.Pin_3, S2.Pin_4, R8.Pin_1
  N3: Part3.GND, R8.Pin_0, Q4.source, R11.Pin_0, R15.Pin_1
  N4: Part3.D3_PWM, Q4.Gate, R11.Pin_1
  N5: Part3.5V, S2.Pin_1, S2.Pin_2, R10.Pin_0
  N6: Q4.drain, U3.+
  N7: R10.Pin_1, D3.C, U3.-
  N8: R15.Pin_0, LED3.anode
