# Fritzing sketch Shield board connection chart (saved by Fritzing 0.8.7b)

parts:
  Part1 = Adafruit Proto Shield R3 [part_number="Adafruit #2077"]
  LED1 = smd LED [color="Yellow (595nm)" package="0805 [SMD]"]
  S1 = Pushbutton [package="[THT]"]
  LED2 = smd LED [color="Green (570nm)" package="1206 [SMD]"]
  JP4 = Header 1 [package=1x01_offset]
  JP5 = Header 1 [package=1x01_offset]
  JP6 = Header 1 [package=1x01_offset]
  JP7 = Header 1 [package=1x01_offset]
  JP8 = Header 1 [package=1x01_offset]
  JP9 = Header 1 [package=1x01_offset]
  JP10 = Header 1 [package=1x01_offset]
  JP11 = Header 1 [package=1x01_offset]
  JP12 = Header 1 [package=1x01_offset]
  JP13 = Header 1 [package=1x01_offset]
  JP14 = Header 1 [package=1x01_offset]
  SEN4 = Pulse Sensor [package=SIP]
  J2 = Basic Force Sensing Resistor (FSR) [package=THT]
  U5 = Vibration Motor- ROB-08449 [package=vibe-motor-10mm]
  U6 = Vibration Motor- ROB-08449 [package=vibe-motor-10mm]

nets:
  N1: Part1.P$5#1, JP14.1, U6.+
  N2: Part1.P$5#118, JP13.1, U6.-
  N3: Part1.1#166, JP12.1, U5.+
  N4: Part1.1#169, JP11.1, U5.-
  N5: Part1.P$6, Part1.+5V, S1.Pin_3, S1.Pin_4
  N6: Part1.N$10, JP10.1
  N7: Part1.N$26, Part1.N$196, S1.Pin_1, S1.Pin_2
  N8: Part1.N$43, JP9.1
  N9: Part1.N$68, LED2.cathode
  N10: Part1.N$69, LED2.anode
  N11: Part1.N$114, JP8.1, J2.pin_0
  N12: Part1.N$119, JP5.1, SEN4.GND
  N13: Part1.N$121, JP7.1, J2.pin_1
  N14: Part1.N$122, JP4.1, SEN4.Vcc
  N15: Part1.N$215, JP6.1, SEN4.Signal
  N16: Part1.N$260, LED1.cathode
  N17: Part1.N$261, LED1.anode

notes:
  EDA sensor goes here.

custom parts:
  Adafruit Proto Shield R3: This prototyping shield is the best out there (well, we think so, at least), and now is even better with Version R3 - updated for the most compatibility with just about all the Arduinos! It works with UNO, Mega, Leonardo, NG, Diecimila, Duemilanove, and compatible Arduinos. Yun's and Arduino Ethernets have a chunky Ethernet jack that gets in the way of stacking, you can use the stacking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
  Pulse Sensor: Pulse Sensor Optical Heart Rate Monitor for Arduino and other microcontrollers
